// Digital circuit cpu.dig as structural Verilog
module cpu (
  input  ACASCADEMOD,
  input  AINMOD,
  input  AENO,
  input  ALUCIN,
  input  ALOAD,
  input  ACLKMOD,
  input  ALUENO,
  input  clk,
  input  AENDEF,
  input  BCASCADEMOD,
  input  BINMOD,
  input  BENO,
  input  BLOAD,
  input  BCLKMOD,
  input  BENDEF,
  input  EN,
  input  D0,
  input  D1,
  input  D2,
  input  D3,
  input  D4,
  input  D5,
  input  D6,
  input  D7,
  input  PCCASCADEMOD,
  input  PCINMOD,
  input  PCENO,
  input  PCLOAD,
  input  PCCLKMOD,
  input  PCENDEF,
  input  MARCASCADEMOD,
  input  MARINMOD,
  input  MARLOAD,
  input  MARCLKMOD,
  input  MARENDEF,
  input  IRLOAD,
  input  IRENO,
  input  RAMENO,
  input  RAMLOAD,
  input  in_40,
  input  in_41,
  input  in_46,
  input  MARENO,
  output out_42,
  output out_43,
  output out_44,
  output out_45,
  output out_47
);

  wire add_1_c_o, add_1_s, add_2_c_o, add_2_s, add_3_c_o, add_3_s, add_4_c_o, add_4_s, add_5_c_o, add_5_s,
       add_6_c_o, add_6_s, add_7_c_o, add_7_s, add_8_s, and_1_out, and_2_out, and_3_out, and_4_out, d_ff_5_q,
       d_ff_6_q, d_ff_7_q, d_ff_8_q, d_ff_9_q, d_ff_10_q, d_ff_11_q, d_ff_12_q, decoder_1_out_0,
       decoder_1_out_1, decoder_1_out_2, decoder_1_out_3, demultiplexer_1_out_1, demultiplexer_1_out_2,
       demultiplexer_1_out_3, demultiplexer_1_out_4, demultiplexer_1_out_5, demultiplexer_1_out_6,
       demultiplexer_1_out_7, jk_ff_1_nq, jk_ff_2_nq, jk_ff_3_nq, jk_ff_4_nq, jk_ff_5_nq, jk_ff_6_nq,
       jk_ff_7_nq, jk_ff_9_nq, jk_ff_9_q, jk_ff_10_nq, jk_ff_10_q, jk_ff_11_nq, jk_ff_11_q, jk_ff_12_nq,
       jk_ff_12_q, jk_ff_13_nq, jk_ff_13_q, jk_ff_14_nq, jk_ff_14_q, jk_ff_15_nq, jk_ff_15_q, jk_ff_16_q,
       jk_ff_17_nq, jk_ff_17_q, jk_ff_18_nq, jk_ff_18_q, jk_ff_19_nq, jk_ff_19_q, jk_ff_20_nq, jk_ff_20_q,
       jk_ff_21_nq, jk_ff_21_q, jk_ff_22_nq, jk_ff_22_q, jk_ff_23_nq, jk_ff_23_q, jk_ff_24_q, jk_ff_25_nq,
       jk_ff_25_q, jk_ff_26_nq, jk_ff_26_q, jk_ff_27_nq, jk_ff_27_q, jk_ff_28_nq, jk_ff_28_q, jk_ff_29_nq,
       jk_ff_29_q, jk_ff_30_nq, jk_ff_30_q, jk_ff_31_nq, jk_ff_31_q, jk_ff_32_q, multiplexer_1_out,
       multiplexer_2_out, multiplexer_3_out, multiplexer_4_out, multiplexer_5_out, multiplexer_6_out,
       multiplexer_7_out, multiplexer_8_out, multiplexer_9_out, multiplexer_10_out, multiplexer_11_out,
       multiplexer_12_out, multiplexer_13_out, multiplexer_14_out, multiplexer_15_out, multiplexer_16_out,
       multiplexer_18_out, multiplexer_19_out, multiplexer_20_out, multiplexer_21_out, multiplexer_22_out,
       multiplexer_23_out, multiplexer_24_out, multiplexer_25_out, multiplexer_26_out, multiplexer_27_out,
       multiplexer_28_out, multiplexer_29_out, multiplexer_30_out, multiplexer_31_out, multiplexer_32_out,
       multiplexer_33_out, multiplexer_34_out, multiplexer_35_out, multiplexer_36_out, multiplexer_37_out,
       multiplexer_38_out, multiplexer_39_out, multiplexer_40_out, multiplexer_41_out, multiplexer_42_out,
       multiplexer_43_out, multiplexer_44_out, multiplexer_45_out, multiplexer_46_out, multiplexer_47_out,
       multiplexer_48_out, multiplexer_49_out, multiplexer_50_out, multiplexer_51_out, multiplexer_52_out,
       multiplexer_53_out, multiplexer_54_out, multiplexer_55_out, multiplexer_56_out, multiplexer_57_out,
       multiplexer_58_out, multiplexer_59_out, multiplexer_60_out, multiplexer_61_out, multiplexer_62_out,
       multiplexer_63_out, multiplexer_64_out, multiplexer_65_out, multiplexer_66_out, multiplexer_67_out,
       multiplexer_68_out, multiplexer_69_out, multiplexer_70_out, multiplexer_71_out, multiplexer_72_out,
       multiplexer_73_out, multiplexer_74_out, multiplexer_75_out, multiplexer_76_out, multiplexer_77_out,
       multiplexer_78_out, multiplexer_79_out, multiplexer_80_out, multiplexer_81_out, multiplexer_82_out,
       multiplexer_83_out, multiplexer_84_out, multiplexer_85_out, multiplexer_86_out, multiplexer_87_out,
       multiplexer_88_out, multiplexer_89_out, multiplexer_90_out, multiplexer_91_out, multiplexer_92_out,
       multiplexer_93_out, multiplexer_94_out, multiplexer_95_out, multiplexer_96_out, multiplexer_97_out,
       multiplexer_98_out, multiplexer_99_out, multiplexer_100_out, multiplexer_101_out, multiplexer_102_out,
       multiplexer_103_out, multiplexer_104_out, multiplexer_105_out, multiplexer_106_out,
       multiplexer_107_out, multiplexer_108_out, multiplexer_109_out, multiplexer_110_out,
       multiplexer_111_out, multiplexer_112_out, multiplexer_113_out, multiplexer_114_out,
       multiplexer_115_out, multiplexer_116_out, multiplexer_117_out, multiplexer_118_out,
       multiplexer_119_out, multiplexer_120_out, multiplexer_121_out, multiplexer_122_out,
       multiplexer_123_out, multiplexer_124_out, multiplexer_125_out, multiplexer_126_out,
       multiplexer_127_out, multiplexer_128_out, multiplexer_129_out, not_1_out, not_2_out, not_3_out,
       not_4_out, not_5_out, not_6_out, not_7_out, not_8_out, not_9_out, not_10_out, not_11_out, or_1_out,
       or_2_out, or_4_out, or_5_out, or_6_out, or_7_out, or_8_out, or_9_out, or_10_out, or_11_out, or_12_out,
       or_13_out, or_14_out, or_15_out, or_16_out, or_17_out, or_18_out, or_19_out, or_20_out, or_21_out,
       or_22_out, or_23_out, or_24_out, or_25_out, or_26_out, or_27_out, or_28_out, or_29_out, undriven,
       undriven_2, undriven_3, undriven_4, undriven_5, undriven_6, undriven_7, undriven_8, undriven_9,
       undriven_10, undriven_11, undriven_12, undriven_13, undriven_14, undriven_15, undriven_16,
       undriven_17, undriven_18, xor_1_out, xor_2_out, xor_3_out, xor_4_out, xor_5_out, xor_6_out, xor_7_out,
       xor_8_out, xor_9_out, xor_10_out, xor_11_out, xor_12_out, xor_13_out, xor_14_out, xor_15_out,
       xor_16_out, xor_17_out, xor_18_out, xor_19_out, xor_20_out, xor_21_out, xor_22_out, xor_23_out,
       xor_24_out, xor_25_out, xor_26_out, xor_27_out, xor_28_out, xor_29_out, xor_30_out, xor_31_out,
       xor_32_out;
  wire [1:0] counter_1_out;
  wire [2:0] or_30_out;
  wire [7:0] driver_11_out, jk_ff_5_q, ramdualport_1_d;

  or or_1 (or_1_out, out_45, in_40);
  not not_1 (not_1_out, clk);
  not not_2 (not_2_out, in_46);
  not not_3 (not_3_out, or_7_out);
  Multiplexer multiplexer_1 (.sel(or_9_out), .in_0(ramdualport_1_d[0]), .in_1(1'b1), .out(multiplexer_1_out));
  Multiplexer multiplexer_2 (.sel(or_9_out), .in_0(ramdualport_1_d[1]), .in_1(1'b1), .out(multiplexer_2_out));
  Multiplexer multiplexer_3 (.sel(or_9_out), .in_0(ramdualport_1_d[2]), .in_1(1'b1), .out(multiplexer_3_out));
  Multiplexer multiplexer_4 (.sel(or_9_out), .in_0(ramdualport_1_d[3]), .in_1(1'b1), .out(multiplexer_4_out));
  Multiplexer multiplexer_5 (.sel(or_9_out), .in_0(ramdualport_1_d[4]), .in_1(1'b1), .out(multiplexer_5_out));
  Multiplexer multiplexer_6 (.sel(or_9_out), .in_0(ramdualport_1_d[5]), .in_1(1'b1), .out(multiplexer_6_out));
  Multiplexer multiplexer_7 (.sel(or_9_out), .in_0(ramdualport_1_d[6]), .in_1(1'b1), .out(multiplexer_7_out));
  Multiplexer multiplexer_8 (.sel(or_9_out), .in_0(ramdualport_1_d[7]), .in_1(1'b1), .out(multiplexer_8_out));
  Counter #(.Bits(2)) counter_1 (.en(in_46), .C(not_1_out), .clr(not_2_out), .out(counter_1_out));  // open: ovf
  and and_1 (and_1_out, decoder_1_out_3, in_46);
  not not_4 (not_4_out, or_8_out);
  or or_2 (or_2_out, not_4_out, not_3_out);
  Multiplexer multiplexer_9 (.sel(or_7_out), .in_0(jk_ff_5_q[0]), .in_1(multiplexer_1_out), .out(multiplexer_9_out));
  Multiplexer multiplexer_10 (.sel(or_7_out), .in_0(jk_ff_5_q[1]), .in_1(multiplexer_2_out), .out(multiplexer_10_out));
  Multiplexer multiplexer_11 (.sel(or_7_out), .in_0(jk_ff_5_q[2]), .in_1(multiplexer_3_out), .out(multiplexer_11_out));
  Multiplexer multiplexer_12 (.sel(or_7_out), .in_0(jk_ff_5_q[3]), .in_1(multiplexer_4_out), .out(multiplexer_12_out));
  Multiplexer multiplexer_13 (.sel(or_7_out), .in_0(jk_ff_5_q[4]), .in_1(multiplexer_5_out), .out(multiplexer_13_out));
  Multiplexer multiplexer_14 (.sel(or_7_out), .in_0(jk_ff_5_q[5]), .in_1(multiplexer_6_out), .out(multiplexer_14_out));
  Multiplexer multiplexer_15 (.sel(or_7_out), .in_0(jk_ff_5_q[6]), .in_1(multiplexer_7_out), .out(multiplexer_15_out));
  Multiplexer multiplexer_16 (.sel(or_7_out), .in_0(jk_ff_5_q[7]), .in_1(multiplexer_8_out), .out(multiplexer_16_out));
  D_FF d_ff_1 (.D(or_1_out), .C(in_41), .Q(out_42));  // open: nQ
  Decoder #(.Selector_Bits(2)) decoder_1 (
    .sel(counter_1_out), .out_0(decoder_1_out_0), .out_1(decoder_1_out_1), .out_2(decoder_1_out_2),
    .out_3(decoder_1_out_3));
  and and_2 (and_2_out, in_46, decoder_1_out_2);
  not not_5 (not_5_out, and_1_out);
  or or_3 (out_47, and_2_out, not_5_out);
  xor xor_1 (xor_1_out, multiplexer_9_out, or_2_out);
  xor xor_2 (xor_2_out, multiplexer_10_out, or_2_out);
  xor xor_3 (xor_3_out, multiplexer_11_out, or_2_out);
  xor xor_4 (xor_4_out, multiplexer_12_out, or_2_out);
  xor xor_5 (xor_5_out, multiplexer_13_out, or_2_out);
  xor xor_6 (xor_6_out, multiplexer_14_out, or_2_out);
  xor xor_7 (xor_7_out, multiplexer_15_out, or_2_out);
  xor xor_8 (xor_8_out, multiplexer_16_out, or_2_out);
  D_FF d_ff_2 (.D(out_42), .C(in_41), .Q(out_43));  // open: nQ
  and and_3 (and_3_out, in_46, decoder_1_out_1);
  D_FF d_ff_3 (.D(out_43), .C(in_41), .Q(out_44));  // open: nQ
  and and_4 (and_4_out, in_46, decoder_1_out_0);
  D_FF d_ff_4 (.D(out_44), .C(in_41), .Q(out_45));  // open: nQ
  Multiplexer #(.Selector_Bits(2)) multiplexer_17 ();  // open: sel, in_0, in_1, in_2, in_3, out
  Multiplexer multiplexer_18 (.sel(or_6_out), .in_0(clk), .in_1(multiplexer_25_out), .out(multiplexer_18_out));
  Multiplexer multiplexer_19 (.sel(or_6_out), .in_0(clk), .in_1(multiplexer_26_out), .out(multiplexer_19_out));
  Multiplexer multiplexer_20 (.sel(or_6_out), .in_0(clk), .in_1(multiplexer_27_out), .out(multiplexer_20_out));
  Multiplexer multiplexer_21 (.sel(or_6_out), .in_0(clk), .in_1(multiplexer_28_out), .out(multiplexer_21_out));
  Multiplexer multiplexer_22 (.sel(or_6_out), .in_0(clk), .in_1(multiplexer_29_out), .out(multiplexer_22_out));
  Multiplexer multiplexer_23 (.sel(or_6_out), .in_0(clk), .in_1(multiplexer_30_out), .out(multiplexer_23_out));
  Multiplexer multiplexer_24 (.sel(or_6_out), .in_0(clk), .in_1(multiplexer_31_out), .out(multiplexer_24_out));
  or or_4 (or_4_out, 1'b0, and_3_out);
  JK_FF jk_ff_1 (.J(multiplexer_9_out), .C(clk), .K(xor_1_out), .Q(jk_ff_5_q[0]), .nQ(jk_ff_1_nq));
  JK_FF jk_ff_2 (.J(multiplexer_10_out), .C(multiplexer_18_out), .K(xor_2_out), .Q(jk_ff_5_q[1]), .nQ(jk_ff_2_nq));
  JK_FF jk_ff_3 (.J(multiplexer_11_out), .C(multiplexer_19_out), .K(xor_3_out), .Q(jk_ff_5_q[2]), .nQ(jk_ff_3_nq));
  JK_FF jk_ff_4 (.J(multiplexer_12_out), .C(multiplexer_20_out), .K(xor_4_out), .Q(jk_ff_5_q[3]), .nQ(jk_ff_4_nq));
  JK_FF jk_ff_5 (.J(multiplexer_13_out), .C(multiplexer_21_out), .K(xor_5_out), .Q(jk_ff_5_q[4]), .nQ(jk_ff_5_nq));
  JK_FF jk_ff_6 (.J(multiplexer_14_out), .C(multiplexer_22_out), .K(xor_6_out), .Q(jk_ff_5_q[5]), .nQ(jk_ff_6_nq));
  JK_FF jk_ff_7 (.J(multiplexer_15_out), .C(multiplexer_23_out), .K(xor_7_out), .Q(jk_ff_5_q[6]), .nQ(jk_ff_7_nq));
  JK_FF jk_ff_8 (.J(multiplexer_16_out), .C(multiplexer_24_out), .K(xor_8_out), .Q(jk_ff_5_q[7]));  // open: nQ
  or or_5 (or_5_out, 1'b0, undriven_18);
  Multiplexer multiplexer_25 (.sel(or_5_out), .in_0(jk_ff_1_nq), .in_1(jk_ff_5_q[0]), .out(multiplexer_25_out));
  Multiplexer multiplexer_26 (.sel(or_5_out), .in_0(jk_ff_2_nq), .in_1(jk_ff_5_q[1]), .out(multiplexer_26_out));
  Multiplexer multiplexer_27 (.sel(or_5_out), .in_0(jk_ff_3_nq), .in_1(jk_ff_5_q[2]), .out(multiplexer_27_out));
  Multiplexer multiplexer_28 (.sel(or_5_out), .in_0(jk_ff_4_nq), .in_1(jk_ff_5_q[3]), .out(multiplexer_28_out));
  Multiplexer multiplexer_29 (.sel(or_5_out), .in_0(jk_ff_5_nq), .in_1(jk_ff_5_q[4]), .out(multiplexer_29_out));
  Multiplexer multiplexer_30 (.sel(or_5_out), .in_0(jk_ff_6_nq), .in_1(jk_ff_5_q[5]), .out(multiplexer_30_out));
  Multiplexer multiplexer_31 (.sel(or_5_out), .in_0(jk_ff_7_nq), .in_1(jk_ff_5_q[6]), .out(multiplexer_31_out));
  RAMDualPort #(.AddrBits(8), .Bits(8)) ramdualport_1 (
    .A(jk_ff_5_q), .Din(driver_11_out), .str(or_10_out), .C(clk), .ld(demultiplexer_1_out_2),
    .D(ramdualport_1_d));
  Multiplexer multiplexer_32 (.sel(or_4_out), .in_0(d_ff_5_q), .in_1(ramdualport_1_d[0]), .out(multiplexer_32_out));
  Multiplexer multiplexer_33 (.sel(or_4_out), .in_0(d_ff_6_q), .in_1(ramdualport_1_d[1]), .out(multiplexer_33_out));
  Multiplexer multiplexer_34 (.sel(or_4_out), .in_0(d_ff_7_q), .in_1(ramdualport_1_d[2]), .out(multiplexer_34_out));
  Multiplexer multiplexer_35 (.sel(or_4_out), .in_0(d_ff_8_q), .in_1(ramdualport_1_d[3]), .out(multiplexer_35_out));
  Multiplexer multiplexer_36 (.sel(or_4_out), .in_0(d_ff_9_q), .in_1(ramdualport_1_d[4]), .out(multiplexer_36_out));
  Multiplexer multiplexer_37 (.sel(or_4_out), .in_0(d_ff_10_q), .in_1(ramdualport_1_d[5]), .out(multiplexer_37_out));
  Multiplexer multiplexer_38 (.sel(or_4_out), .in_0(d_ff_11_q), .in_1(ramdualport_1_d[6]), .out(multiplexer_38_out));
  Multiplexer multiplexer_39 (.sel(or_4_out), .in_0(d_ff_12_q), .in_1(ramdualport_1_d[7]), .out(multiplexer_39_out));
  or or_6 (or_6_out, 1'b0, undriven_17);
  or or_7 (or_7_out, 1'b0, and_4_out);
  assign ramdualport_1_d[0] = demultiplexer_1_out_3 ? jk_ff_5_q[0] : 1'bz;  // Driver driver_1
  assign ramdualport_1_d[1] = demultiplexer_1_out_3 ? jk_ff_5_q[1] : 1'bz;  // Driver driver_2
  assign ramdualport_1_d[2] = demultiplexer_1_out_3 ? jk_ff_5_q[2] : 1'bz;  // Driver driver_3
  assign ramdualport_1_d[3] = demultiplexer_1_out_3 ? jk_ff_5_q[3] : 1'bz;  // Driver driver_4
  assign ramdualport_1_d[4] = demultiplexer_1_out_3 ? jk_ff_5_q[4] : 1'bz;  // Driver driver_5
  assign ramdualport_1_d[5] = demultiplexer_1_out_3 ? jk_ff_5_q[5] : 1'bz;  // Driver driver_6
  assign ramdualport_1_d[6] = demultiplexer_1_out_3 ? jk_ff_5_q[6] : 1'bz;  // Driver driver_7
  assign ramdualport_1_d[7] = demultiplexer_1_out_3 ? jk_ff_5_q[7] : 1'bz;  // Driver driver_8
  D_FF d_ff_5 (.D(multiplexer_32_out), .C(clk), .Q(d_ff_5_q));  // open: nQ
  D_FF d_ff_6 (.D(multiplexer_33_out), .C(clk), .Q(d_ff_6_q));  // open: nQ
  D_FF d_ff_7 (.D(multiplexer_34_out), .C(clk), .Q(d_ff_7_q));  // open: nQ
  D_FF d_ff_8 (.D(multiplexer_35_out), .C(clk), .Q(d_ff_8_q));  // open: nQ
  D_FF d_ff_9 (.D(multiplexer_36_out), .C(clk), .Q(d_ff_9_q));  // open: nQ
  D_FF d_ff_10 (.D(multiplexer_37_out), .C(clk), .Q(d_ff_10_q));  // open: nQ
  D_FF d_ff_11 (.D(multiplexer_38_out), .C(clk), .Q(d_ff_11_q));  // open: nQ
  D_FF d_ff_12 (.D(multiplexer_39_out), .C(clk), .Q(d_ff_12_q));  // open: nQ
  or or_8 (or_8_out, 1'b0, undriven_16);
  LED led_1 (.in(d_ff_12_q));
  or or_9 (or_9_out, 1'b0, undriven_15);
  LED led_2 (.in(d_ff_11_q));
  LED led_3 (.in(d_ff_10_q));
  or or_10 (or_10_out, 1'b0, undriven_14);
  LED led_4 (.in(jk_ff_5_q[7]));
  LED led_5 (.in(d_ff_9_q));
  LED led_6 (.in(d_ff_8_q));
  or or_11 (or_11_out, 1'b0, and_3_out);
  LED led_7 (.in(jk_ff_5_q[5]));
  LED led_8 (.in(jk_ff_5_q[6]));
  assign driver_11_out[7] = or_10_out ? ramdualport_1_d[7] : 1'bz;  // Driver driver_9
  assign driver_11_out[6] = or_10_out ? ramdualport_1_d[6] : 1'bz;  // Driver driver_10
  assign driver_11_out[5] = or_10_out ? ramdualport_1_d[5] : 1'bz;  // Driver driver_11
  assign driver_11_out[4] = or_10_out ? ramdualport_1_d[4] : 1'bz;  // Driver driver_12
  assign driver_11_out[3] = or_10_out ? ramdualport_1_d[3] : 1'bz;  // Driver driver_13
  assign driver_11_out[2] = or_10_out ? ramdualport_1_d[2] : 1'bz;  // Driver driver_14
  assign driver_11_out[1] = or_10_out ? ramdualport_1_d[1] : 1'bz;  // Driver driver_15
  assign driver_11_out[0] = or_10_out ? ramdualport_1_d[0] : 1'bz;  // Driver driver_16
  LED led_9 (.in(d_ff_6_q));
  LED led_10 (.in(d_ff_7_q));
  or or_12 (or_12_out, 1'b0, and_3_out);
  or or_13 (or_13_out, 1'b0, and_3_out);
  LED led_11 (.in(jk_ff_5_q[4]));
  LED led_12 (.in(jk_ff_5_q[3]));
  LED led_13 (.in(d_ff_5_q));
  assign ramdualport_1_d[0] = demultiplexer_1_out_1 ? d_ff_5_q : 1'bz;  // Driver driver_17
  assign ramdualport_1_d[1] = demultiplexer_1_out_1 ? d_ff_6_q : 1'bz;  // Driver driver_18
  assign ramdualport_1_d[2] = demultiplexer_1_out_1 ? d_ff_7_q : 1'bz;  // Driver driver_19
  assign ramdualport_1_d[3] = demultiplexer_1_out_1 ? d_ff_8_q : 1'bz;  // Driver driver_20
  assign ramdualport_1_d[4] = demultiplexer_1_out_1 ? 1'b0 : 1'bz;  // Driver driver_21
  assign ramdualport_1_d[5] = demultiplexer_1_out_1 ? 1'b0 : 1'bz;  // Driver driver_22
  assign ramdualport_1_d[6] = demultiplexer_1_out_1 ? 1'b0 : 1'bz;  // Driver driver_23
  assign ramdualport_1_d[7] = demultiplexer_1_out_1 ? 1'b0 : 1'bz;  // Driver driver_24
  or or_14 (or_14_out, 1'b0, and_3_out);
  LED led_14 (.in(jk_ff_5_q[2]));
  LED led_15 (.in(jk_ff_5_q[1]));
  or or_15 (or_15_out, 1'b0, undriven_13);
  LED led_16 (.in(jk_ff_5_q[0]));
  or or_16 (or_16_out, 1'b0, undriven_12);
  LED led_17 (.in(ramdualport_1_d[6]));
  LED led_18 (.in(ramdualport_1_d[7]));
  or or_17 (or_17_out, 1'b0, undriven_11);
  LED led_19 (.in(ramdualport_1_d[4]));
  LED led_20 (.in(ramdualport_1_d[5]));
  or or_18 (or_18_out, 1'b0, undriven_10);
  or or_19 (or_19_out, 1'b0, undriven_9);
  LED led_21 (.in(ramdualport_1_d[3]));
  LED led_22 (.in(ramdualport_1_d[2]));
  or or_20 (or_20_out, 1'b0, undriven_8);
  LED led_23 (.in(ramdualport_1_d[1]));
  LED led_24 (.in(ramdualport_1_d[0]));
  or or_21 (or_21_out, 1'b0, undriven_7);
  assign ramdualport_1_d[7] = EN ? D7 : 1'bz;  // Driver driver_25
  assign ramdualport_1_d[6] = EN ? D6 : 1'bz;  // Driver driver_26
  assign ramdualport_1_d[5] = EN ? D5 : 1'bz;  // Driver driver_27
  or or_22 (or_22_out, 1'b0, undriven_6);
  or or_23 (or_23_out, 1'b0, undriven);
  assign ramdualport_1_d[4] = EN ? D4 : 1'bz;  // Driver driver_28
  assign ramdualport_1_d[3] = EN ? D3 : 1'bz;  // Driver driver_29
  Multiplexer multiplexer_40 (.sel(or_11_out), .in_0(ramdualport_1_d[0]), .in_1(1'b1), .out(multiplexer_40_out));
  Multiplexer multiplexer_41 (.sel(or_11_out), .in_0(ramdualport_1_d[1]), .in_1(1'b1), .out(multiplexer_41_out));
  Multiplexer multiplexer_42 (.sel(or_11_out), .in_0(ramdualport_1_d[2]), .in_1(1'b1), .out(multiplexer_42_out));
  Multiplexer multiplexer_43 (.sel(or_11_out), .in_0(ramdualport_1_d[3]), .in_1(1'b1), .out(multiplexer_43_out));
  Multiplexer multiplexer_44 (.sel(or_11_out), .in_0(ramdualport_1_d[4]), .in_1(1'b1), .out(multiplexer_44_out));
  Multiplexer multiplexer_45 (.sel(or_11_out), .in_0(ramdualport_1_d[5]), .in_1(1'b1), .out(multiplexer_45_out));
  Multiplexer multiplexer_46 (.sel(or_11_out), .in_0(ramdualport_1_d[6]), .in_1(1'b1), .out(multiplexer_46_out));
  Multiplexer multiplexer_47 (.sel(or_11_out), .in_0(ramdualport_1_d[7]), .in_1(1'b1), .out(multiplexer_47_out));
  Multiplexer multiplexer_48 (.sel(or_16_out), .in_0(ramdualport_1_d[0]), .in_1(1'b1), .out(multiplexer_48_out));
  Multiplexer multiplexer_49 (.sel(or_16_out), .in_0(ramdualport_1_d[1]), .in_1(1'b1), .out(multiplexer_49_out));
  Multiplexer multiplexer_50 (.sel(or_16_out), .in_0(ramdualport_1_d[2]), .in_1(1'b1), .out(multiplexer_50_out));
  Multiplexer multiplexer_51 (.sel(or_16_out), .in_0(ramdualport_1_d[3]), .in_1(1'b1), .out(multiplexer_51_out));
  Multiplexer multiplexer_52 (.sel(or_16_out), .in_0(ramdualport_1_d[4]), .in_1(1'b1), .out(multiplexer_52_out));
  Multiplexer multiplexer_53 (.sel(or_16_out), .in_0(ramdualport_1_d[5]), .in_1(1'b1), .out(multiplexer_53_out));
  Multiplexer multiplexer_54 (.sel(or_16_out), .in_0(ramdualport_1_d[6]), .in_1(1'b1), .out(multiplexer_54_out));
  Multiplexer multiplexer_55 (.sel(or_16_out), .in_0(ramdualport_1_d[7]), .in_1(1'b1), .out(multiplexer_55_out));
  Multiplexer multiplexer_56 (.sel(or_22_out), .in_0(ramdualport_1_d[0]), .in_1(1'b1), .out(multiplexer_56_out));
  Multiplexer multiplexer_57 (.sel(or_22_out), .in_0(ramdualport_1_d[1]), .in_1(1'b1), .out(multiplexer_57_out));
  Multiplexer multiplexer_58 (.sel(or_22_out), .in_0(ramdualport_1_d[2]), .in_1(1'b1), .out(multiplexer_58_out));
  Multiplexer multiplexer_59 (.sel(or_22_out), .in_0(ramdualport_1_d[3]), .in_1(1'b1), .out(multiplexer_59_out));
  Multiplexer multiplexer_60 (.sel(or_22_out), .in_0(ramdualport_1_d[4]), .in_1(1'b1), .out(multiplexer_60_out));
  Multiplexer multiplexer_61 (.sel(or_22_out), .in_0(ramdualport_1_d[5]), .in_1(1'b1), .out(multiplexer_61_out));
  Multiplexer multiplexer_62 (.sel(or_22_out), .in_0(ramdualport_1_d[6]), .in_1(1'b1), .out(multiplexer_62_out));
  Multiplexer multiplexer_63 (.sel(or_22_out), .in_0(ramdualport_1_d[7]), .in_1(1'b1), .out(multiplexer_63_out));
  or or_24 (or_24_out, 1'b0, undriven_2);
  assign ramdualport_1_d[2] = EN ? D2 : 1'bz;  // Driver driver_30
  assign ramdualport_1_d[1] = EN ? D1 : 1'bz;  // Driver driver_31
  not not_6 (not_6_out, or_12_out);
  not not_7 (not_7_out, or_13_out);
  or or_25 (or_25_out, not_6_out, not_7_out);
  not not_8 (not_8_out, or_17_out);
  not not_9 (not_9_out, or_18_out);
  or or_26 (or_26_out, not_8_out, not_9_out);
  not not_10 (not_10_out, or_23_out);
  not not_11 (not_11_out, or_24_out);
  or or_27 (or_27_out, not_10_out, not_11_out);
  or or_28 (or_28_out, 1'b0, undriven_3);
  assign ramdualport_1_d[0] = EN ? D0 : 1'bz;  // Driver driver_32
  Multiplexer multiplexer_64 (.sel(or_13_out), .in_0(jk_ff_9_q), .in_1(multiplexer_40_out), .out(multiplexer_64_out));
  Multiplexer multiplexer_65 (.sel(or_13_out), .in_0(jk_ff_10_q), .in_1(multiplexer_41_out), .out(multiplexer_65_out));
  Multiplexer multiplexer_66 (.sel(or_13_out), .in_0(jk_ff_11_q), .in_1(multiplexer_42_out), .out(multiplexer_66_out));
  Multiplexer multiplexer_67 (.sel(or_13_out), .in_0(jk_ff_12_q), .in_1(multiplexer_43_out), .out(multiplexer_67_out));
  Multiplexer multiplexer_68 (.sel(or_13_out), .in_0(jk_ff_13_q), .in_1(multiplexer_44_out), .out(multiplexer_68_out));
  Multiplexer multiplexer_69 (.sel(or_13_out), .in_0(jk_ff_14_q), .in_1(multiplexer_45_out), .out(multiplexer_69_out));
  Multiplexer multiplexer_70 (.sel(or_13_out), .in_0(jk_ff_15_q), .in_1(multiplexer_46_out), .out(multiplexer_70_out));
  Multiplexer multiplexer_71 (.sel(or_13_out), .in_0(jk_ff_16_q), .in_1(multiplexer_47_out), .out(multiplexer_71_out));
  Multiplexer multiplexer_72 (.sel(or_18_out), .in_0(jk_ff_17_q), .in_1(multiplexer_48_out), .out(multiplexer_72_out));
  Multiplexer multiplexer_73 (.sel(or_18_out), .in_0(jk_ff_18_q), .in_1(multiplexer_49_out), .out(multiplexer_73_out));
  Multiplexer multiplexer_74 (.sel(or_18_out), .in_0(jk_ff_19_q), .in_1(multiplexer_50_out), .out(multiplexer_74_out));
  Multiplexer multiplexer_75 (.sel(or_18_out), .in_0(jk_ff_20_q), .in_1(multiplexer_51_out), .out(multiplexer_75_out));
  Multiplexer multiplexer_76 (.sel(or_18_out), .in_0(jk_ff_21_q), .in_1(multiplexer_52_out), .out(multiplexer_76_out));
  Multiplexer multiplexer_77 (.sel(or_18_out), .in_0(jk_ff_22_q), .in_1(multiplexer_53_out), .out(multiplexer_77_out));
  Multiplexer multiplexer_78 (.sel(or_18_out), .in_0(jk_ff_23_q), .in_1(multiplexer_54_out), .out(multiplexer_78_out));
  Multiplexer multiplexer_79 (.sel(or_18_out), .in_0(jk_ff_24_q), .in_1(multiplexer_55_out), .out(multiplexer_79_out));
  Multiplexer multiplexer_80 (.sel(or_24_out), .in_0(jk_ff_25_q), .in_1(multiplexer_56_out), .out(multiplexer_80_out));
  Multiplexer multiplexer_81 (.sel(or_24_out), .in_0(jk_ff_26_q), .in_1(multiplexer_57_out), .out(multiplexer_81_out));
  Multiplexer multiplexer_82 (.sel(or_24_out), .in_0(jk_ff_27_q), .in_1(multiplexer_58_out), .out(multiplexer_82_out));
  Multiplexer multiplexer_83 (.sel(or_24_out), .in_0(jk_ff_28_q), .in_1(multiplexer_59_out), .out(multiplexer_83_out));
  Multiplexer multiplexer_84 (.sel(or_24_out), .in_0(jk_ff_29_q), .in_1(multiplexer_60_out), .out(multiplexer_84_out));
  Multiplexer multiplexer_85 (.sel(or_24_out), .in_0(jk_ff_30_q), .in_1(multiplexer_61_out), .out(multiplexer_85_out));
  Multiplexer multiplexer_86 (.sel(or_24_out), .in_0(jk_ff_31_q), .in_1(multiplexer_62_out), .out(multiplexer_86_out));
  Multiplexer multiplexer_87 (.sel(or_24_out), .in_0(jk_ff_32_q), .in_1(multiplexer_63_out), .out(multiplexer_87_out));
  or or_29 (or_29_out, 1'b0, undriven_4);
  xor xor_9 (xor_9_out, multiplexer_64_out, or_25_out);
  xor xor_10 (xor_10_out, multiplexer_65_out, or_25_out);
  xor xor_11 (xor_11_out, multiplexer_66_out, or_25_out);
  xor xor_12 (xor_12_out, multiplexer_67_out, or_25_out);
  xor xor_13 (xor_13_out, multiplexer_68_out, or_25_out);
  xor xor_14 (xor_14_out, multiplexer_69_out, or_25_out);
  xor xor_15 (xor_15_out, multiplexer_70_out, or_25_out);
  xor xor_16 (xor_16_out, multiplexer_71_out, or_25_out);
  xor xor_17 (xor_17_out, multiplexer_72_out, or_26_out);
  xor xor_18 (xor_18_out, multiplexer_73_out, or_26_out);
  xor xor_19 (xor_19_out, multiplexer_74_out, or_26_out);
  xor xor_20 (xor_20_out, multiplexer_75_out, or_26_out);
  xor xor_21 (xor_21_out, multiplexer_76_out, or_26_out);
  xor xor_22 (xor_22_out, multiplexer_77_out, or_26_out);
  xor xor_23 (xor_23_out, multiplexer_78_out, or_26_out);
  xor xor_24 (xor_24_out, multiplexer_79_out, or_26_out);
  xor xor_25 (xor_25_out, multiplexer_80_out, or_27_out);
  xor xor_26 (xor_26_out, multiplexer_81_out, or_27_out);
  xor xor_27 (xor_27_out, multiplexer_82_out, or_27_out);
  xor xor_28 (xor_28_out, multiplexer_83_out, or_27_out);
  xor xor_29 (xor_29_out, multiplexer_84_out, or_27_out);
  xor xor_30 (xor_30_out, multiplexer_85_out, or_27_out);
  xor xor_31 (xor_31_out, multiplexer_86_out, or_27_out);
  xor xor_32 (xor_32_out, multiplexer_87_out, or_27_out);
  or or_30 (or_30_out[2], 1'b0, and_4_out);
  Demultiplexer #(.Selector_Bits(3)) demultiplexer_1 (
    .sel(or_30_out), .in(1'b1), .out_1(demultiplexer_1_out_1), .out_2(demultiplexer_1_out_2),
    .out_3(demultiplexer_1_out_3), .out_4(demultiplexer_1_out_4), .out_5(demultiplexer_1_out_5),
    .out_6(demultiplexer_1_out_6), .out_7(demultiplexer_1_out_7));  // open: out_0
  or or_31 (or_30_out[1], 1'b0, and_3_out);
  Multiplexer multiplexer_88 (.sel(or_14_out), .in_0(clk), .in_1(multiplexer_109_out), .out(multiplexer_88_out));
  Multiplexer multiplexer_89 (.sel(or_14_out), .in_0(clk), .in_1(multiplexer_110_out), .out(multiplexer_89_out));
  Multiplexer multiplexer_90 (.sel(or_14_out), .in_0(clk), .in_1(multiplexer_111_out), .out(multiplexer_90_out));
  Multiplexer multiplexer_91 (.sel(or_14_out), .in_0(clk), .in_1(multiplexer_112_out), .out(multiplexer_91_out));
  Multiplexer multiplexer_92 (.sel(or_14_out), .in_0(clk), .in_1(multiplexer_113_out), .out(multiplexer_92_out));
  Multiplexer multiplexer_93 (.sel(or_14_out), .in_0(clk), .in_1(multiplexer_114_out), .out(multiplexer_93_out));
  Multiplexer multiplexer_94 (.sel(or_14_out), .in_0(clk), .in_1(multiplexer_115_out), .out(multiplexer_94_out));
  Multiplexer multiplexer_95 (.sel(or_19_out), .in_0(clk), .in_1(multiplexer_116_out), .out(multiplexer_95_out));
  Multiplexer multiplexer_96 (.sel(or_19_out), .in_0(clk), .in_1(multiplexer_117_out), .out(multiplexer_96_out));
  Multiplexer multiplexer_97 (.sel(or_19_out), .in_0(clk), .in_1(multiplexer_118_out), .out(multiplexer_97_out));
  Multiplexer multiplexer_98 (.sel(or_19_out), .in_0(clk), .in_1(multiplexer_119_out), .out(multiplexer_98_out));
  Multiplexer multiplexer_99 (.sel(or_19_out), .in_0(clk), .in_1(multiplexer_120_out), .out(multiplexer_99_out));
  Multiplexer multiplexer_100 (.sel(or_19_out), .in_0(clk), .in_1(multiplexer_121_out), .out(multiplexer_100_out));
  Multiplexer multiplexer_101 (.sel(or_19_out), .in_0(clk), .in_1(multiplexer_122_out), .out(multiplexer_101_out));
  Add add_1 (.a(jk_ff_17_q), .b(jk_ff_25_q), .c_i(or_21_out), .s(add_1_s), .c_o(add_1_c_o));
  Add add_2 (.a(jk_ff_19_q), .b(jk_ff_27_q), .c_i(add_5_c_o), .s(add_2_s), .c_o(add_2_c_o));
  Add add_3 (.a(jk_ff_21_q), .b(jk_ff_29_q), .c_i(add_6_c_o), .s(add_3_s), .c_o(add_3_c_o));
  Add add_4 (.a(jk_ff_23_q), .b(jk_ff_31_q), .c_i(add_7_c_o), .s(add_4_s), .c_o(add_4_c_o));
  Multiplexer multiplexer_102 (.sel(or_28_out), .in_0(clk), .in_1(multiplexer_123_out), .out(multiplexer_102_out));
  Multiplexer multiplexer_103 (.sel(or_28_out), .in_0(clk), .in_1(multiplexer_124_out), .out(multiplexer_103_out));
  Multiplexer multiplexer_104 (.sel(or_28_out), .in_0(clk), .in_1(multiplexer_125_out), .out(multiplexer_104_out));
  Multiplexer multiplexer_105 (.sel(or_28_out), .in_0(clk), .in_1(multiplexer_126_out), .out(multiplexer_105_out));
  Multiplexer multiplexer_106 (.sel(or_28_out), .in_0(clk), .in_1(multiplexer_127_out), .out(multiplexer_106_out));
  Multiplexer multiplexer_107 (.sel(or_28_out), .in_0(clk), .in_1(multiplexer_128_out), .out(multiplexer_107_out));
  Multiplexer multiplexer_108 (.sel(or_28_out), .in_0(clk), .in_1(multiplexer_129_out), .out(multiplexer_108_out));
  or or_32 (or_30_out[0], 1'b0, undriven_5);
  JK_FF jk_ff_9 (.J(multiplexer_64_out), .C(clk), .K(xor_9_out), .Q(jk_ff_9_q), .nQ(jk_ff_9_nq));
  JK_FF jk_ff_10 (.J(multiplexer_65_out), .C(multiplexer_88_out), .K(xor_10_out), .Q(jk_ff_10_q), .nQ(jk_ff_10_nq));
  JK_FF jk_ff_11 (.J(multiplexer_66_out), .C(multiplexer_89_out), .K(xor_11_out), .Q(jk_ff_11_q), .nQ(jk_ff_11_nq));
  JK_FF jk_ff_12 (.J(multiplexer_67_out), .C(multiplexer_90_out), .K(xor_12_out), .Q(jk_ff_12_q), .nQ(jk_ff_12_nq));
  JK_FF jk_ff_13 (.J(multiplexer_68_out), .C(multiplexer_91_out), .K(xor_13_out), .Q(jk_ff_13_q), .nQ(jk_ff_13_nq));
  JK_FF jk_ff_14 (.J(multiplexer_69_out), .C(multiplexer_92_out), .K(xor_14_out), .Q(jk_ff_14_q), .nQ(jk_ff_14_nq));
  JK_FF jk_ff_15 (.J(multiplexer_70_out), .C(multiplexer_93_out), .K(xor_15_out), .Q(jk_ff_15_q), .nQ(jk_ff_15_nq));
  JK_FF jk_ff_16 (.J(multiplexer_71_out), .C(multiplexer_94_out), .K(xor_16_out), .Q(jk_ff_16_q));  // open: nQ
  JK_FF jk_ff_17 (.J(multiplexer_72_out), .C(clk), .K(xor_17_out), .Q(jk_ff_17_q), .nQ(jk_ff_17_nq));
  JK_FF jk_ff_18 (.J(multiplexer_73_out), .C(multiplexer_95_out), .K(xor_18_out), .Q(jk_ff_18_q), .nQ(jk_ff_18_nq));
  JK_FF jk_ff_19 (.J(multiplexer_74_out), .C(multiplexer_96_out), .K(xor_19_out), .Q(jk_ff_19_q), .nQ(jk_ff_19_nq));
  JK_FF jk_ff_20 (.J(multiplexer_75_out), .C(multiplexer_97_out), .K(xor_20_out), .Q(jk_ff_20_q), .nQ(jk_ff_20_nq));
  JK_FF jk_ff_21 (.J(multiplexer_76_out), .C(multiplexer_98_out), .K(xor_21_out), .Q(jk_ff_21_q), .nQ(jk_ff_21_nq));
  JK_FF jk_ff_22 (.J(multiplexer_77_out), .C(multiplexer_99_out), .K(xor_22_out), .Q(jk_ff_22_q), .nQ(jk_ff_22_nq));
  JK_FF jk_ff_23 (.J(multiplexer_78_out), .C(multiplexer_100_out), .K(xor_23_out), .Q(jk_ff_23_q), .nQ(jk_ff_23_nq));
  JK_FF jk_ff_24 (.J(multiplexer_79_out), .C(multiplexer_101_out), .K(xor_24_out), .Q(jk_ff_24_q));  // open: nQ
  Add add_5 (.a(jk_ff_18_q), .b(jk_ff_26_q), .c_i(add_1_c_o), .s(add_5_s), .c_o(add_5_c_o));
  Add add_6 (.a(jk_ff_20_q), .b(jk_ff_28_q), .c_i(add_2_c_o), .s(add_6_s), .c_o(add_6_c_o));
  Add add_7 (.a(jk_ff_22_q), .b(jk_ff_30_q), .c_i(add_3_c_o), .s(add_7_s), .c_o(add_7_c_o));
  Add add_8 (.a(jk_ff_24_q), .b(jk_ff_32_q), .c_i(add_4_c_o), .s(add_8_s));  // open: c_o
  JK_FF jk_ff_25 (.J(multiplexer_80_out), .C(clk), .K(xor_25_out), .Q(jk_ff_25_q), .nQ(jk_ff_25_nq));
  JK_FF jk_ff_26 (.J(multiplexer_81_out), .C(multiplexer_102_out), .K(xor_26_out), .Q(jk_ff_26_q), .nQ(jk_ff_26_nq));
  JK_FF jk_ff_27 (.J(multiplexer_82_out), .C(multiplexer_103_out), .K(xor_27_out), .Q(jk_ff_27_q), .nQ(jk_ff_27_nq));
  JK_FF jk_ff_28 (.J(multiplexer_83_out), .C(multiplexer_104_out), .K(xor_28_out), .Q(jk_ff_28_q), .nQ(jk_ff_28_nq));
  JK_FF jk_ff_29 (.J(multiplexer_84_out), .C(multiplexer_105_out), .K(xor_29_out), .Q(jk_ff_29_q), .nQ(jk_ff_29_nq));
  JK_FF jk_ff_30 (.J(multiplexer_85_out), .C(multiplexer_106_out), .K(xor_30_out), .Q(jk_ff_30_q), .nQ(jk_ff_30_nq));
  JK_FF jk_ff_31 (.J(multiplexer_86_out), .C(multiplexer_107_out), .K(xor_31_out), .Q(jk_ff_31_q), .nQ(jk_ff_31_nq));
  JK_FF jk_ff_32 (.J(multiplexer_87_out), .C(multiplexer_108_out), .K(xor_32_out), .Q(jk_ff_32_q));  // open: nQ
  Multiplexer multiplexer_109 (.sel(or_15_out), .in_0(jk_ff_9_nq), .in_1(jk_ff_9_q), .out(multiplexer_109_out));
  Multiplexer multiplexer_110 (.sel(or_15_out), .in_0(jk_ff_10_nq), .in_1(jk_ff_10_q), .out(multiplexer_110_out));
  Multiplexer multiplexer_111 (.sel(or_15_out), .in_0(jk_ff_11_nq), .in_1(jk_ff_11_q), .out(multiplexer_111_out));
  Multiplexer multiplexer_112 (.sel(or_15_out), .in_0(jk_ff_12_nq), .in_1(jk_ff_12_q), .out(multiplexer_112_out));
  Multiplexer multiplexer_113 (.sel(or_15_out), .in_0(jk_ff_13_nq), .in_1(jk_ff_13_q), .out(multiplexer_113_out));
  Multiplexer multiplexer_114 (.sel(or_15_out), .in_0(jk_ff_14_nq), .in_1(jk_ff_14_q), .out(multiplexer_114_out));
  Multiplexer multiplexer_115 (.sel(or_15_out), .in_0(jk_ff_15_nq), .in_1(jk_ff_15_q), .out(multiplexer_115_out));
  Multiplexer multiplexer_116 (.sel(or_20_out), .in_0(jk_ff_17_nq), .in_1(jk_ff_17_q), .out(multiplexer_116_out));
  Multiplexer multiplexer_117 (.sel(or_20_out), .in_0(jk_ff_18_nq), .in_1(jk_ff_18_q), .out(multiplexer_117_out));
  Multiplexer multiplexer_118 (.sel(or_20_out), .in_0(jk_ff_19_nq), .in_1(jk_ff_19_q), .out(multiplexer_118_out));
  Multiplexer multiplexer_119 (.sel(or_20_out), .in_0(jk_ff_20_nq), .in_1(jk_ff_20_q), .out(multiplexer_119_out));
  Multiplexer multiplexer_120 (.sel(or_20_out), .in_0(jk_ff_21_nq), .in_1(jk_ff_21_q), .out(multiplexer_120_out));
  Multiplexer multiplexer_121 (.sel(or_20_out), .in_0(jk_ff_22_nq), .in_1(jk_ff_22_q), .out(multiplexer_121_out));
  Multiplexer multiplexer_122 (.sel(or_20_out), .in_0(jk_ff_23_nq), .in_1(jk_ff_23_q), .out(multiplexer_122_out));
  assign ramdualport_1_d[0] = demultiplexer_1_out_6 ? add_1_s : 1'bz;  // Driver driver_33
  assign ramdualport_1_d[1] = demultiplexer_1_out_6 ? add_5_s : 1'bz;  // Driver driver_34
  assign ramdualport_1_d[2] = demultiplexer_1_out_6 ? add_2_s : 1'bz;  // Driver driver_35
  assign ramdualport_1_d[3] = demultiplexer_1_out_6 ? add_6_s : 1'bz;  // Driver driver_36
  assign ramdualport_1_d[4] = demultiplexer_1_out_6 ? add_3_s : 1'bz;  // Driver driver_37
  assign ramdualport_1_d[5] = demultiplexer_1_out_6 ? add_7_s : 1'bz;  // Driver driver_38
  assign ramdualport_1_d[6] = demultiplexer_1_out_6 ? add_4_s : 1'bz;  // Driver driver_39
  assign ramdualport_1_d[7] = demultiplexer_1_out_6 ? add_8_s : 1'bz;  // Driver driver_40
  Multiplexer multiplexer_123 (.sel(or_29_out), .in_0(jk_ff_25_nq), .in_1(jk_ff_25_q), .out(multiplexer_123_out));
  Multiplexer multiplexer_124 (.sel(or_29_out), .in_0(jk_ff_26_nq), .in_1(jk_ff_26_q), .out(multiplexer_124_out));
  Multiplexer multiplexer_125 (.sel(or_29_out), .in_0(jk_ff_27_nq), .in_1(jk_ff_27_q), .out(multiplexer_125_out));
  Multiplexer multiplexer_126 (.sel(or_29_out), .in_0(jk_ff_28_nq), .in_1(jk_ff_28_q), .out(multiplexer_126_out));
  Multiplexer multiplexer_127 (.sel(or_29_out), .in_0(jk_ff_29_nq), .in_1(jk_ff_29_q), .out(multiplexer_127_out));
  Multiplexer multiplexer_128 (.sel(or_29_out), .in_0(jk_ff_30_nq), .in_1(jk_ff_30_q), .out(multiplexer_128_out));
  Multiplexer multiplexer_129 (.sel(or_29_out), .in_0(jk_ff_31_nq), .in_1(jk_ff_31_q), .out(multiplexer_129_out));
  assign ramdualport_1_d[0] = demultiplexer_1_out_4 ? jk_ff_9_q : 1'bz;  // Driver driver_41
  assign ramdualport_1_d[1] = demultiplexer_1_out_4 ? jk_ff_10_q : 1'bz;  // Driver driver_42
  assign ramdualport_1_d[2] = demultiplexer_1_out_4 ? jk_ff_11_q : 1'bz;  // Driver driver_43
  assign ramdualport_1_d[3] = demultiplexer_1_out_4 ? jk_ff_12_q : 1'bz;  // Driver driver_44
  assign ramdualport_1_d[4] = demultiplexer_1_out_4 ? jk_ff_13_q : 1'bz;  // Driver driver_45
  assign ramdualport_1_d[5] = demultiplexer_1_out_4 ? jk_ff_14_q : 1'bz;  // Driver driver_46
  assign ramdualport_1_d[6] = demultiplexer_1_out_4 ? jk_ff_15_q : 1'bz;  // Driver driver_47
  assign ramdualport_1_d[7] = demultiplexer_1_out_4 ? jk_ff_16_q : 1'bz;  // Driver driver_48
  assign ramdualport_1_d[0] = demultiplexer_1_out_5 ? jk_ff_17_q : 1'bz;  // Driver driver_49
  assign ramdualport_1_d[1] = demultiplexer_1_out_5 ? jk_ff_18_q : 1'bz;  // Driver driver_50
  assign ramdualport_1_d[2] = demultiplexer_1_out_5 ? jk_ff_19_q : 1'bz;  // Driver driver_51
  assign ramdualport_1_d[3] = demultiplexer_1_out_5 ? jk_ff_20_q : 1'bz;  // Driver driver_52
  assign ramdualport_1_d[4] = demultiplexer_1_out_5 ? jk_ff_21_q : 1'bz;  // Driver driver_53
  assign ramdualport_1_d[5] = demultiplexer_1_out_5 ? jk_ff_22_q : 1'bz;  // Driver driver_54
  assign ramdualport_1_d[6] = demultiplexer_1_out_5 ? jk_ff_23_q : 1'bz;  // Driver driver_55
  assign ramdualport_1_d[7] = demultiplexer_1_out_5 ? jk_ff_24_q : 1'bz;  // Driver driver_56
  assign ramdualport_1_d[0] = demultiplexer_1_out_7 ? jk_ff_25_q : 1'bz;  // Driver driver_57
  assign ramdualport_1_d[1] = demultiplexer_1_out_7 ? jk_ff_26_q : 1'bz;  // Driver driver_58
  assign ramdualport_1_d[2] = demultiplexer_1_out_7 ? jk_ff_27_q : 1'bz;  // Driver driver_59
  assign ramdualport_1_d[3] = demultiplexer_1_out_7 ? jk_ff_28_q : 1'bz;  // Driver driver_60
  assign ramdualport_1_d[4] = demultiplexer_1_out_7 ? jk_ff_29_q : 1'bz;  // Driver driver_61
  assign ramdualport_1_d[5] = demultiplexer_1_out_7 ? jk_ff_30_q : 1'bz;  // Driver driver_62
  assign ramdualport_1_d[6] = demultiplexer_1_out_7 ? jk_ff_31_q : 1'bz;  // Driver driver_63
  assign ramdualport_1_d[7] = demultiplexer_1_out_7 ? jk_ff_32_q : 1'bz;  // Driver driver_64
  LED led_25 (.in(jk_ff_16_q));
  LED led_26 (.in(jk_ff_24_q));
  LED led_27 (.in(add_8_s));
  LED led_28 (.in(jk_ff_32_q));
  LED led_29 (.in(jk_ff_14_q));
  LED led_30 (.in(jk_ff_15_q));
  LED led_31 (.in(jk_ff_22_q));
  LED led_32 (.in(jk_ff_23_q));
  LED led_33 (.in(add_4_s));
  LED led_34 (.in(add_7_s));
  LED led_35 (.in(jk_ff_30_q));
  LED led_36 (.in(jk_ff_31_q));
  LED led_37 (.in(jk_ff_13_q));
  LED led_38 (.in(jk_ff_12_q));
  LED led_39 (.in(jk_ff_21_q));
  LED led_40 (.in(jk_ff_20_q));
  LED led_41 (.in(add_3_s));
  LED led_42 (.in(add_6_s));
  LED led_43 (.in(jk_ff_29_q));
  LED led_44 (.in(jk_ff_28_q));
  LED led_45 (.in(jk_ff_11_q));
  LED led_46 (.in(jk_ff_10_q));
  LED led_47 (.in(jk_ff_19_q));
  LED led_48 (.in(jk_ff_18_q));
  LED led_49 (.in(add_2_s));
  LED led_50 (.in(add_5_s));
  LED led_51 (.in(jk_ff_27_q));
  LED led_52 (.in(jk_ff_26_q));
  LED led_53 (.in(jk_ff_9_q));
  LED led_54 (.in(jk_ff_17_q));
  LED led_55 (.in(add_1_s));
  LED led_56 (.in(jk_ff_25_q));

  // Notes on the sheet:
  //   DEF
  //   IR
  //   MAR
  //   Poor man's multiplexer
  //   Register A
  //   Register B
  //   PC
  //   ALU
endmodule
